# Fritzing sketch usbremote (saved by Fritzing 0.9.3b)
breadboards: 1

parts:
  U1 = atmega328 [package=dip]
  IR_reciever = TSOP312.., 314.. [part_number="TSOP 2438" package=THT]
  pulldown = Resistor [tolerance=±5% resistance=1M package="0402 [SMD]"]
  Crystal = Crystal [frequency="20 MHz" package=SMD]
  C1 = Tantalum Capacitor [capacitance=2.2µF package="100 mil [THT, tantalum]"]
  C2 = Tantalum Capacitor [capacitance=2.2µF package="100 mil [THT, tantalum]"]
  R3 = Resistor [tolerance=±5% resistance=6.8k package=THT]
  R2 = Resistor [tolerance=±5% resistance=6.8k package=THT]
  USB = USB connector [package=THT]
  part = Resistor [tolerance=±5% resistance=1.5k package=THT]

nets:
  N1: U1.D2, R3.Pin_1
  N2: U1.D3_(PWM), part.Pin_1
  N3: U1.D4, R2.Pin_1
  VCC: U1.VCC, IR_reciever.Vs, USB.5V
  GND: U1.GND#7, IR_reciever.GND, pulldown.Pin_0, C1.+, C2.+, USB.GND, USB.chassis5, USB.chassis6
  N4: U1.XLAT1, Crystal.pin_0, C2.-
  N5: U1.XLAT2, Crystal.pin_1, C1.-
  N6: U1.D8, IR_reciever.Data, pulldown.Pin_1
  N7: R3.Pin_0, USB.d-, part.Pin_0
  N8: R2.Pin_0, USB.d+
